# Fritzing sketch CNC editable PCB Layout_fritzing file (saved by Fritzing 0.9.3b)
circuit board: 8.94061cm x 5.09689cm

parts:
  L293D = L293D [package=THT]
  5-9VDC = Screw terminal - 2 pins [package=THT]
  M1 = Screw terminal - 2 pins [package=THT]
  M2 = Screw terminal - 2 pins [package=THT]
  M3 = Screw terminal - 2 pins [package=THT]
  L293D_2 = L293D [package=THT]
  M4 = Screw terminal - 2 pins [package=THT]
  SERVO = male alternating pin header, 3 pins [form="♂ (male)"]
  Arduino_nano = Arduino Nano (Rev3.0) (ICSP)

nets:
  N1: L293D.Enable_1, L293D.Enable_2, L293D.+V, L293D_2.Enable_1, L293D_2.Enable_2, L293D_2.+V, SERVO.pin2, Arduino_nano.5V
  N2: L293D.In_1, Arduino_nano.D8
  N3: L293D.Out_1_(_Controlled_by_Enable_1_), M3.pin1
  N4: L293D.0V, 5-9VDC.pin2, L293D_2.0V, SERVO.pin1, Arduino_nano.GND
  N5: L293D.Out_2_(_Controlled_by_Enable_1_), M3.pin2
  N6: L293D.In_2, Arduino_nano.D9
  N7: L293D.+Vmotor, 5-9VDC.pin1, L293D_2.+Vmotor
  N8: L293D.In_3, Arduino_nano.D10
  N9: L293D.Out_3_(_Controlled_by_Enable_2_), M4.pin2
  N10: L293D.Out_4_(_Controlled_by_Enable_2_), M4.pin1
  N11: L293D.In_4, Arduino_nano.D11/MOSI
  N12: M1.pin1, L293D_2.Out_4_(_Controlled_by_Enable_2_)
  N13: M1.pin2, L293D_2.Out_3_(_Controlled_by_Enable_2_)
  N14: M2.pin1, L293D_2.Out_1_(_Controlled_by_Enable_1_)
  N15: M2.pin2, L293D_2.Out_2_(_Controlled_by_Enable_1_)
  N16: L293D_2.In_1, Arduino_nano.D5
  N17: L293D_2.In_2, Arduino_nano.D4
  N18: L293D_2.In_3, Arduino_nano.D3
  N19: L293D_2.In_4, Arduino_nano.D2
  N20: SERVO.pin3, Arduino_nano.D6

notes:
  cnc plotter pcb by T.A.Vignesh
  +  -
